# Fritzing sketch wiremap (saved by Fritzing 0.9.4)
breadboards: 1

parts:
  U1 = LCD-16X2 [package=lcd-16x2]
  MCU1 = Raspberry Pi Zero
  R1 = Trimmer Potentiometer [maximum_resistance=10kΩ package=THT]
  JP1 = Header 10 [package=1x10-2mm-smd]  # not connected

nets:
  N1: U1.VSS, U1.VO, U1.R_W, U1.K, MCU1.pin_6, MCU1.pin_34, MCU1.pin_39
  N2: U1.VDD, MCU1.pin_2, MCU1.pin_4, R1.wiper
  N3: U1.RS, MCU1.pin_7
  N4: U1.E, MCU1.pin_11
  N5: U1.DB4, MCU1.pin_12
  N6: U1.DB5, MCU1.pin_15
  N7: U1.DB6, MCU1.pin_16
  N8: U1.DB7, MCU1.pin_18
  N9: U1.A, R1.leg1, R1.leg2
